// Logisim project ChamAlanLogisim.circ as structural Verilog: 8 circuits, main circuit LCD
module LCD (
  input  A,
  input  B,
  input  C,
  input  D
);

  wire horizontal_bottom_1_out, horizontal_mid_1_out, horizontal_top_1_out, vertical_bottomleft_1_out,
       vertical_bottomright_1_out, vertical_topleft_1_out, vertical_topright_1_out;

  Horizontal_Mid horizontal_mid_1 (.A(A), .B(B), .C(C), .D(D), .Out(horizontal_mid_1_out));
  _7_Segment_Display u_7_segment_display_1 (
    .g(horizontal_mid_1_out), .f(vertical_topleft_1_out), .a(horizontal_top_1_out),
    .b(vertical_topright_1_out), .e(vertical_bottomleft_1_out), .d(horizontal_bottom_1_out),
    .c(vertical_bottomright_1_out));  // open: dp
  Vertical_BottomLeft vertical_bottomleft_1 (.A(A), .B(B), .C(C), .D(D), .Out(vertical_bottomleft_1_out));
  Horizontal_Top horizontal_top_1 (.A(A), .B(B), .C(C), .D(D), .Out(horizontal_top_1_out));
  Vertical_TopLeft vertical_topleft_1 (.A(A), .B(B), .C(C), .D(D), .Out(vertical_topleft_1_out));
  Horizontal_Bottom horizontal_bottom_1 (.A(A), .B(B), .C(C), .D(D), .Out(horizontal_bottom_1_out));
  Vertical_BottomRight vertical_bottomright_1 (.A(A), .B(B), .C(C), .D(D), .Out(vertical_bottomright_1_out));
  Vertical_TopRight vertical_topright_1 (.A(A), .B(B), .C(C), .D(D), .Out(vertical_topright_1_out));
endmodule

module Horizontal_Top (
  input  A,
  input  B,
  input  C,
  input  D,
  output Out
);

  wire and_1_out, and_2_out, not_1_out, not_2_out;

  or or_1 (Out, A, C, and_1_out, and_2_out);
  and and_1 (and_1_out, B, D);
  not not_1 (not_1_out, B);
  not not_2 (not_2_out, D);
  and and_2 (and_2_out, not_1_out, not_2_out);
endmodule

module Horizontal_Mid (
  input  A,
  input  B,
  input  C,
  input  D,
  output Out
);

  wire and_1_out, and_2_out, and_3_out, not_1_out, not_2_out;

  not not_1 (not_1_out, B);
  and and_1 (and_1_out, not_1_out, C);
  or or_1 (Out, A, and_1_out, and_3_out);
  and and_2 (and_2_out, C, D);
  and and_3 (and_3_out, B, not_2_out);
  not not_2 (not_2_out, and_2_out);
endmodule

module Horizontal_Bottom (
  input  A,
  input  B,
  input  C,
  input  D,
  output Out
);

  wire and_1_out, and_2_out, and_3_out, and_4_out, not_1_out, not_2_out, not_3_out, not_4_out, not_5_out;

  not not_1 (not_1_out, B);
  and and_1 (and_1_out, C, not_1_out);
  not not_2 (not_2_out, D);
  not not_3 (not_3_out, B);
  and and_2 (and_2_out, not_3_out, not_2_out);
  or or_1 (Out, A, and_1_out, and_2_out, and_3_out, and_4_out);
  not not_4 (not_4_out, C);
  and and_3 (and_3_out, B, not_4_out, D);
  not not_5 (not_5_out, D);
  and and_4 (and_4_out, C, not_5_out);
endmodule

module Vertical_TopLeft (
  input  A,
  input  B,
  input  C,
  input  D,
  output Out
);

  wire and_1_out, and_2_out, and_3_out, not_1_out, not_2_out, not_3_out, not_4_out;

  not not_1 (not_1_out, C);
  and and_1 (and_1_out, B, not_1_out);
  or or_1 (Out, A, and_1_out, and_2_out, and_3_out);
  not not_2 (not_2_out, C);
  not not_3 (not_3_out, D);
  and and_2 (and_2_out, B, not_3_out);
  and and_3 (and_3_out, not_2_out, not_4_out);
  not not_4 (not_4_out, D);
endmodule

module Vertical_TopRight (
  input  A,
  input  B,
  input  C,
  input  D,
  output Out
);

  wire and_1_out, and_2_out, not_1_out, not_2_out, not_3_out;

  not not_1 (not_1_out, B);
  or or_1 (Out, not_1_out, and_1_out, and_2_out);
  not not_2 (not_2_out, C);
  and and_1 (and_1_out, C, D);
  and and_2 (and_2_out, not_2_out, not_3_out);
  not not_3 (not_3_out, D);
endmodule

module Vertical_BottomLeft (
  input  A,
  input  B,
  input  C,
  input  D,
  output Out
);

  wire not_1_out, not_2_out, or_1_out;

  not not_1 (not_1_out, B);
  or or_1 (or_1_out, not_1_out, C);
  and and_1 (Out, or_1_out, not_2_out);
  not not_2 (not_2_out, D);
endmodule

module Vertical_BottomRight (
  input  A,
  input  B,
  input  C,
  input  D,
  output Out
);

  wire and_1_out, and_2_out, not_1_out, not_2_out;

  not not_1 (not_1_out, A);
  and and_1 (and_1_out, not_1_out, B);
  not not_2 (not_2_out, C);
  or or_1 (Out, and_1_out, not_2_out, and_2_out);
  and and_2 (and_2_out, C, D);
endmodule
